# Fritzing sketch Wiring Diagram (saved by Fritzing 0.9.6b)
breadboards: 1

parts:
  Arduino_Nano_33_IOT = Arduino Nano 33 BLE Sense
  PART2 = Sound Detector
  MQ-3_Gas_Sensor_(Alcohol) = MQ-3 breakout
  RGB_Sound_Meter = RGB LED (com. cathode, rgb) [package="5 mm [THT]"]
  RGB_Alcohol = RGB LED (com. cathode, rgb) [package="5 mm [THT]"]
  R1 = Resistor [tolerance=±5% power=0.25 resistance=220 package=THT]
  R2 = Resistor [tolerance=±5% power=0.25 resistance=220 package=THT]
  R3 = Resistor [tolerance=±5% power=0.25 resistance=220 package=THT]
  R4 = Resistor [tolerance=±5% power=0.25 resistance=220 package=THT]
  R5 = Resistor [tolerance=±5% power=0.25 resistance=220 package=THT]
  R6 = Resistor [tolerance=±5% power=0.25 resistance=220 package=THT]

nets:
  GND: Arduino_Nano_33_IOT.GND, Arduino_Nano_33_IOT.A7, PART2.GND, MQ-3_Gas_Sensor_(Alcohol).GND, RGB_Sound_Meter.common_cathode, RGB_Alcohol.common_cathode
  N1: Arduino_Nano_33_IOT.D2, R6.Pin_1
  N2: Arduino_Nano_33_IOT.D3~, R5.Pin_1
  N3: Arduino_Nano_33_IOT.D4, R4.Pin_1
  N4: Arduino_Nano_33_IOT.D5~, R3.Pin_1
  N5: Arduino_Nano_33_IOT.D6~, R2.Pin_1
  N6: Arduino_Nano_33_IOT.D7, R1.Pin_1
  +5V: Arduino_Nano_33_IOT.D11/MOSI, Arduino_Nano_33_IOT.+5V, MQ-3_Gas_Sensor_(Alcohol).VCC
  N7: Arduino_Nano_33_IOT.A2, PART2.ENVELOPE
  N8: Arduino_Nano_33_IOT.A1, MQ-3_Gas_Sensor_(Alcohol).DO
  N9: Arduino_Nano_33_IOT.A0, MQ-3_Gas_Sensor_(Alcohol).AO
  3V3: Arduino_Nano_33_IOT.3V3, PART2.VCC
  N10: RGB_Sound_Meter.red_anode, R3.Pin_0
  N11: RGB_Sound_Meter.green_anode, R2.Pin_0
  N12: RGB_Sound_Meter.blue_anode, R1.Pin_0
  N13: RGB_Alcohol.red_anode, R6.Pin_0
  N14: RGB_Alcohol.green_anode, R5.Pin_0
  N15: RGB_Alcohol.blue_anode, R4.Pin_0

custom parts:
  Arduino Nano 33 BLE Sense: The Nano 33 BLE Sense (without headers) is Arduino’s 3.3V AI enabled board in the smallest available form factor: 45x18mm! The Arduino Nano 33 BLE Sense is a completely new board on a well-known form factor. It comes with a series of embedded sensors: 9 axis inertial sensor: what makes this board ideal for wearable devices humidity, and temperature sensor: to get highly accurate measurements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
  Sound Detector: Electret microphone with multiple outputs. - First output is the actual audio - Second output is the amplitude envelope - Third output is a binary "sound present" indication - high while sound is present, low otherwise. Visit sparkfun.com for more documentations.
  MQ-3 breakout: Alcohol sensor is capable of detecting alcohol (ethanol) particles on itself and gives the information in digital form back to us to manipulate with it. SKU:101251 • Voltage: 5V DC • Power: max 750mW • Measurement range: 0.04-4mg/L
